// Logisim project DMUX.circ as structural Verilog: 1 circuit, main circuit main
module main (
  input  cin,
  input  sel,
  output a,
  output b
);

  wire not_1_out;

  not not_1 (not_1_out, sel);
  and and_1 (a, cin, not_1_out);
  and and_2 (b, cin, sel);
endmodule
